# Fritzing sketch microbit and ldr example (saved by Fritzing 0.9.3b)

parts:
  R1 = Photocell (LDR) [package=THT]
  R2 = Resistor [tolerance=±5% resistance=10k package=THT]
  Micro_bit1 = Microbit

nets:
  N1: R1.pin_0, Micro_bit1.GND
  N2: R2.Pin_0, Micro_bit1.0
  N3: R2.Pin_1, Micro_bit1.3V

custom parts:
  Microbit: BBC Microbit Fritzing part
