# Fritzing sketch microbit and neopixel example (saved by Fritzing 0.9.3b)

parts:
  R3 = BBC MicroBit
  Part1 = NeoPixel Stick [part_number=1426]

nets:
  GND: R3.GND, Part1.GND
  3V3: R3.3v3, Part1.+5V
  N1: R3.P0_ANALOG_IN, Part1.DATAIN

custom parts:
  BBC MicroBit: The BBC MICRO:BIT
  NeoPixel Stick: Make your own little LED strip arrangement with this stick of NeoPixel LEDs. We crammed 8 of the tiny 5050 (5mm x 5mm) smart RGB LEDs onto a PCB with mounting holes and a chainable design. Use only one microcontroller pin to control as many as you can chain together! Each LED is addressable as the driver chip is inside the LED. Each one has ~18mA constant current drive so the color will be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
