# Fritzing sketch microbit and rgb led example (saved by Fritzing 0.9.3b)

parts:
  R2 = Resistor [tolerance=±5% resistance=1k package=THT]
  LED1 = RGB LED (com. cathode, rgb) [package="5 mm [THT]"]
  R3 = BBC MicroBit
  R4 = Resistor [tolerance=±5% resistance=1k package=THT]
  R5 = Resistor [tolerance=±5% resistance=1k package=THT]

nets:
  N1: R2.Pin_0, LED1.red_anode
  N2: R2.Pin_1, R3.P0_ANALOG_IN
  N3: LED1.common_cathode, R3.GND
  N4: LED1.green_anode, R4.Pin_0
  N5: LED1.blue_anode, R5.Pin_0
  N6: R3.P2_-_ANALOG_IN, R5.Pin_1
  N7: R3.P1_ANALOG_IN, R4.Pin_1

custom parts:
  BBC MicroBit: The BBC MICRO:BIT
